# Fritzing sketch TimerBT_A (saved by Fritzing 0.9.3b)
breadboards: 1

parts:
  元件4 = Arduino Uno (Rev3) - ICSP
  元件5 = Bluetooth HC-05 Macho
  LED1 = LED - 5mm [color="Red (633nm)" package="5 mm [THT]"]
  LED2 = LED - 5mm [color="Green (555nm)" package="5 mm [THT]"]
  Grove1 = Grove Button

nets:
  N1: 元件4.ICSP_MOSI, 元件4.D11_PWM/MOSI, 元件5.RXD
  N2: 元件4.D8, LED2.anode
  N3: 元件4.D10_PWM/SS, 元件5.TXD
  GND: 元件4.GND, 元件5.GND, LED1.cathode, LED2.cathode, Grove1.GND
  N4: 元件4.D2, Grove1.SIG
  N5: 元件4.D7, LED1.anode
  3V3: 元件4.3V3, Grove1.VCC
  5V: 元件4.5V, 元件5.VCC
